# Fritzing sketch connections (saved by Fritzing 1.0.5)
breadboards: 1

parts:
  V1 = DC Power Supply [voltage=5V internal_resistance=1Ω max_current=6A]
  J1 = Basic Servo
  J3 = Basic Servo
  M1 = Dagu DGServo 9g (Top view) [part_number=RS001B]
  Part2 = Adafruit INA219 [part_number="Adafruit #904"]
  J4 = Basic Servo
  Mod1 = Raspberry Pi 4B

nets:
  VCC: V1.Pin_2, J1.vcc, M1.vcc, Part2.VIN+, J4.vcc
  GND: V1.Pin_1, J1.gnd, J3.gnd, M1.gnd, Part2.GND, J4.gnd, Mod1.GND
  N1: J1.pulse, Mod1.GPIO6
  N2: J3.vcc, Part2.VIN-
  N3: J3.pulse, Mod1.GPIO12
  N4: M1.pulse, Mod1.GPIO5
  VCC_2: Part2.VCC, Mod1.3V3
  N5: Part2.SDA, Mod1.GPIO2
  N6: Part2.SCL, Mod1.GPIO3
  N7: J4.pulse, Mod1.GPIO13

custom parts:
  Adafruit INA219: This breakout board will solve all your power-monitoring problems. Instead of struggling with two multimeters, you can just use the handy INA219B chip on this breakout to both measure both the high side voltage and DC current draw over I2C with 1% precision. Most current-measuring devices such as our current panel meter are only good for low side measuring. That means that unless you want to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
